# Fritzing sketch robotikaProjekt (saved by Fritzing 0.9.9b)
breadboards: 1

parts:
  Arduino_Micro = Arduino Micro (Rev3)
  Piezzo_Speaker = Piezo Speaker
  R1 = Resistor [tolerance=±5% resistance=220 package="0603 [SMD]"]
  LED1 = LED - 5mm [color="Red (633nm)" current=0.030 package="5 mm [THT]"]
  LED2 = LED - 5mm [color="Green (570nm)" current=0.030 package="5 mm [THT]"]
  R2 = Resistor [tolerance=±5% resistance=220 package="1206 [SMD]"]
  LCD_1602_I2C = LCD1602-I2C
  S1 = Pushbutton [package="[THT]"]
  S3 = Pushbutton [package="[THT]"]
  S4 = Pushbutton [package="[THT]"]
  R3 = Resistor [tolerance=±5% resistance=10k package="0805 [SMD]"]
  R4 = Resistor [tolerance=±5% resistance=10k package="0805 [SMD]"]
  R5 = Resistor [tolerance=±5% resistance=10k package="0805 [SMD]"]
  R6 = Resistor [tolerance=±5% resistance=10k package="0805 [SMD]"]
  S2 = Pushbutton [package="[THT]"]
  SEN1 = Pulse Sensor [package=SIP-3]

nets:
  GND: Arduino_Micro.GND, Piezzo_Speaker.pin1, LED1.cathode, LED2.cathode, LCD_1602_I2C.GND, R3.Pin_1, R4.Pin_1, R5.Pin_1, R6.Pin_1, SEN1.Signal
  N1: Arduino_Micro.D2/SDA, LCD_1602_I2C.SDA
  N2: Arduino_Micro.D3/SCL, LCD_1602_I2C.SCL
  N3: Arduino_Micro.D6_PWM/A7, S3.Pin_1, S3.Pin_2, S4.Pin_1, S4.Pin_2, R5.Pin_0, R6.Pin_0
  N4: Arduino_Micro.D7, R4.Pin_0, S2.Pin_1, S2.Pin_2
  N5: Arduino_Micro.D8_PWM/A8, S1.Pin_1, S1.Pin_2, R3.Pin_0
  N6: Arduino_Micro.D9_PWM/A9, R1.Pin_0
  N7: Arduino_Micro.D10_PWM/A10, R2.Pin_0
  N8: Arduino_Micro.D11_PWM, Piezzo_Speaker.pin2
  VCC: Arduino_Micro.5V, LCD_1602_I2C.VCC, S1.Pin_3, S1.Pin_4, S3.Pin_3, S3.Pin_4, S4.Pin_3, S4.Pin_4, S2.Pin_3, S2.Pin_4, SEN1.VCC
  N9: Arduino_Micro.A0, SEN1.GND
  N10: R1.Pin_1, LED1.anode
  N11: LED2.anode, R2.Pin_1

custom parts:
  LCD1602-I2C: A standard character display, usually with 2x16 characters. Comes in many colors with LCM1602 IIC attached.
  Pulse Sensor: Pulse Sensor Optical Heart Beat Sensor
